// Logisim project problem1.circ as structural Verilog: 1 circuit, main circuit main
module main (
);

  wire button_1_out, clock_1_out, comparator_1_gt, comparator_2_eq;
  wire [4:0] adder_1_out, adder_2_out, register_1_q, subtractor_1_out;
  wire [31:0] adder_3_out, registerfile_1_p1, registerfile_1_p7, registerfile_1_p8;

  Clock clock_1 (.out(clock_1_out));
  Register #(.width(5)) register_1 (
    .D(adder_1_out), .en(1'b1), .clk(clock_1_out), .Q(register_1_q), .clr(button_1_out));
  Button button_1 (.out(button_1_out));
  Adder #(.width(5)) adder_1 (.a(5'b00001), .b(register_1_q), .out(adder_1_out));  // open: cin, cout
  Comparator #(.width(5), .mode("unsigned")) comparator_1 (
    .a(5'b10100), .b(register_1_q), .gt(comparator_1_gt));  // open: eq, lt
  Adder #(.width(5)) adder_2 (.a(5'b00001), .b(register_1_q), .out(adder_2_out));  // open: cin, cout
  Subtractor #(.width(5)) subtractor_1 (.a(register_1_q), .b(5'b00001), .out(subtractor_1_out));  // open: bin, bout
  // RegisterFile registerfile_1: pin names not known; wires that end beside it: registerfile_1_p1, clock_1_out, comparator_1_gt, adder_2_out, register_1_q, subtractor_1_out, registerfile_1_p7, registerfile_1_p8
  Multiplexer #(.width(32), .enable("false")) multiplexer_1 (
    .in0(adder_3_out), .in1(32'h1), .out(registerfile_1_p1), .sel(comparator_2_eq));
  Adder #(.width(32)) adder_3 (.a(registerfile_1_p7), .b(registerfile_1_p8), .out(adder_3_out));  // open: cin, cout
  Comparator #(.width(5)) comparator_2 (.a(register_1_q), .b({5{1'b0}}), .eq(comparator_2_eq));  // open: gt, lt
endmodule
