// Logisim project problem2.circ as structural Verilog: 3 circuits, main circuit main
module main (
);

  wire button_1_out, clock_1_out, comparator_1_gt, step3_1_out_7, step12_1_out_5, step12_2_out_5;
  wire [4:0] adder_1_out, adder_2_out, register_1_q, step3_1_out_6, step12_1_out_4, step12_2_out_4;
  wire [31:0] bit_extender_1_out, multiplier_1_out, step3_1_out_5;

  Clock clock_1 (.out(clock_1_out));
  Register #(.width(5), .trigger("falling")) register_1 (
    .D(adder_1_out), .en(1'b1), .clk(clock_1_out), .Q(register_1_q), .clr(button_1_out));
  Button button_1 (.out(button_1_out));
  Adder #(.width(5)) adder_1 (.a(5'b00001), .b(register_1_q), .out(adder_1_out));  // open: cin, cout
  Comparator #(.width(5), .mode("unsigned")) comparator_1 (
    .a(5'b10101), .b(register_1_q), .gt(comparator_1_gt));  // open: eq, lt
  step12 step12_1 (
    .in_1(clock_1_out), .in_2(register_1_q), .in_3(comparator_1_gt), .out_4(step12_1_out_4),
    .out_5(step12_1_out_5));
  Adder #(.width(5)) adder_2 (.a(5'b00001), .b(step12_1_out_4), .out(adder_2_out));  // open: cin, cout
  step12 step12_2 (
    .in_1(clock_1_out), .in_2(adder_2_out), .in_3(step12_1_out_5), .out_4(step12_2_out_4),
    .out_5(step12_2_out_5));
  assign bit_extender_1_out = {{27{1'b0}}, step12_2_out_4};  // Bit_Extender bit_extender_1
  Multiplier #(.width(32)) multiplier_1 (.a(bit_extender_1_out), .b(32'h5), .out(multiplier_1_out));  // open: cin, cout
  step3 step3_1 (
    .in_1(clock_1_out), .in_2(multiplier_1_out), .in_3(step12_2_out_4), .in_4(step12_2_out_5),
    .out_5(step3_1_out_5), .out_6(step3_1_out_6), .out_7(step3_1_out_7));
  // RegisterFile #(.trigger("falling")) registerfile_1: pin names not known; wires that end beside it: step3_1_out_5, clock_1_out, step3_1_out_7, step3_1_out_6

  // Notes on the sheet:
  //   Check 20
endmodule

module step12 (
  input  in_1,
  input  [4:0] in_2,
  input  in_3,
  output [4:0] out_4,
  output out_5
);

  Register #(.width(5)) register_1 (.D(in_2), .en(1'b1), .clk(in_1), .Q(out_4));  // open: clr
  Register #(.width(1)) register_2 (.D(in_3), .en(1'b1), .clk(in_1), .Q(out_5));  // open: clr
endmodule

module step3 (
  input  in_1,
  input  [31:0] in_2,
  input  [4:0] in_3,
  input  in_4,
  output [31:0] out_5,
  output [4:0] out_6,
  output out_7
);

  Register #(.width(32)) register_1 (.D(in_2), .en(1'b1), .clk(in_1), .Q(out_5));  // open: clr
  Register #(.width(5)) register_2 (.D(in_3), .en(1'b1), .clk(in_1), .Q(out_6));  // open: clr
  Register #(.width(1)) register_3 (.D(in_4), .en(1'b1), .clk(in_1), .Q(out_7));  // open: clr
endmodule
