// Logisim project MIPS_add.circ as structural Verilog: 1 circuit, main circuit main
module main (
);

  wire and_1_out, and_2_out, button_1_out, Clk_out, comparator_1_eq;
  wire [3:0] mips_alu_1_p3;
  wire [4:0] multiplexer_2_out;
  wire [5:0] adder_2_out, bit_extender_1_out, mipsprogramrom_1_p2_2, multiplexer_4_out;
  wire [7:0] mips_alu_1_p4_2;
  wire [10:0] ControlUnit_data;
  wire [23:0] mips_alu_1_p4;
  wire [25:0] mipsprogramrom_1_p2;
  wire [31:0] adder_1_out, bit_extender_2_out, mips_ram_1_p6, multiplexer_1_out, multiplexer_3_out, PC_q,
       registerfile_1_p1, registerfile_1_p7, registerfile_1_p8, shifter_1_out;

  Clock Clk (.out(Clk_out));
  ROM #(.addrWidth(6), .dataWidth(11)) ControlUnit (.addr(mipsprogramrom_1_p2_2), .data(ControlUnit_data));
  Register #(.width(32)) PC (.D(multiplexer_1_out), .en(1'b1), .clk(Clk_out), .Q(PC_q), .clr(button_1_out));
  Button button_1 (.out(button_1_out));
  Adder #(.width(32)) adder_1 (.a(32'h4), .b(PC_q), .out(adder_1_out));  // open: cin, cout
  Multiplexer #(.width(32), .enable("false")) multiplexer_1 (
    .in0(adder_1_out), .in1(shifter_1_out), .out(multiplexer_1_out), .sel(and_1_out));
  and and_1 (and_1_out, ControlUnit_data[4], comparator_1_eq);
  // MIPSProgramROM mipsprogramrom_1: pin names not known; wires that end beside it: PC_q, {mipsprogramrom_1_p2_2, mipsprogramrom_1_p2}, ControlUnit_data[3]
  Multiplexer #(.width(5), .enable("false")) multiplexer_2 (
    .in0(mipsprogramrom_1_p2[20:16]), .in1(mipsprogramrom_1_p2[15:11]), .out(multiplexer_2_out),
    .sel(ControlUnit_data[10]));
  assign bit_extender_1_out = {{3{1'b0}}, ControlUnit_data[2:0]};  // Bit_Extender bit_extender_1
  Comparator #(.width(32)) comparator_1 (
    .a(registerfile_1_p7), .b(registerfile_1_p8), .eq(comparator_1_eq));  // open: gt, lt
  // RegisterFile registerfile_1: pin names not known; wires that end beside it: registerfile_1_p1, Clk_out, ControlUnit_data[7], multiplexer_2_out, mipsprogramrom_1_p2[25:21], mipsprogramrom_1_p2[20:16], registerfile_1_p7, registerfile_1_p8
  assign bit_extender_2_out = {{16{mipsprogramrom_1_p2[15]}}, mipsprogramrom_1_p2[15:0]};  // Bit_Extender bit_extender_2
  Multiplexer #(.width(32), .enable("false")) multiplexer_3 (
    .in0(registerfile_1_p8), .in1(bit_extender_2_out), .out(multiplexer_3_out), .sel(ControlUnit_data[9]));
  Shifter #(.width(32)) shifter_1 (.in(bit_extender_2_out), .\dist (5'b00010), .out(shifter_1_out));
  Adder #(.width(6)) adder_2 (.a(6'b100000), .b(bit_extender_1_out), .out(adder_2_out));  // open: cin, cout
  and and_2 (and_2_out, mipsprogramrom_1_p2_2[0], 1'b1);
  // Mips_ALU mips_alu_1: pin names not known; wires that end beside it: registerfile_1_p7, multiplexer_3_out, mips_alu_1_p3, {mips_alu_1_p4_2, mips_alu_1_p4}
  ROM #(.addrWidth(6), .dataWidth(4)) ALUcontrol (.addr(multiplexer_4_out), .data(mips_alu_1_p3));
  Multiplexer #(.width(6), .enable("false")) multiplexer_4 (
    .in0(mipsprogramrom_1_p2[5:0]), .in1(adder_2_out), .out(multiplexer_4_out), .sel(and_2_out));
  // MIPS_RAM #(.addrWidth(24)) mips_ram_1: pin names not known; wires that end beside it: mips_alu_1_p4, registerfile_1_p8, ControlUnit_data[5], Clk_out, ControlUnit_data[6], mips_ram_1_p6, ControlUnit_data[8]
  Multiplexer #(.width(32), .enable("false")) multiplexer_5 (
    .in0({mips_alu_1_p4_2, mips_alu_1_p4}), .in1(mips_ram_1_p6), .out(registerfile_1_p1),
    .sel(ControlUnit_data[8]));

  // Notes on the sheet:
  //   contents of ControlUnit (hex, n*v repeats v):
  //   482 0 8 0 17 18 0 0 280 281 0 0 284 285 286 20*0 3c0 7*0 220
  //   contents of mipsprogramrom_1 (hex, n*v repeats v):
  //   # addiu , $t1 and $t2 must have value are 1 and 2 addiu $t1, $zero, 1 addiu $t2, $zero, 1  # sw ,
  //   word address (24bit) 1 in RAM  = 1  sw $t1, 0($zero)  # lw, $t3 = 1 lw $t3, 0($zero)  # andi, word
  //   address (24 bits) 1  = 1 andi $t4, $zero, 1 sw $t4, 1($zero)  # ori, word address 2 = 1 ori $t4,
  //   $zero, 1 sw $t4, 2($zero)  # xori, word address 3 = 0 ori $t4, $zero, 1 sw $t4, 3($zero)  # slti,
  //   word address 4 = 0  slti $t4, $t1, 0 sw $t4, 4($zero)  # sltiu, word address 5 = 1 sltiu $t4, $zero,
  //   1 sw $t4, 5($zero)  # addu , word address 6 = 1 addu $t4, $t1, $t2 sw $t4, 6($zero)  # subu, word
  //   address 7 = 2  addiu $t4, $t1, 2 subu $t4, $t4, $t1  sw $t4, 7($zero)  # and, word address 8 = 1 and
  //   $t4, $t1, $t1 sw $t4, 8($zero)  # or, word address 9 = 1  or $t4, $t1, $t1 sw $t4, 9($zero)  # xor,
  //   word address 10 = 1 xor $t4, $zero, $zero sw $t4, 10($zero)  # nor, word address 11 = 1 nor $t4,
  //   $zero, $zero sw $t4, 11($zero)  # slt, word address 12 = 0 slt $t4, $t1, $t1 sw $t4, 12($zero)  #
  //   sltu, word address 13 = 1  sltu $t4, $zero, $t1 sw $t4, 13($zero)  # sll, word address 14 = 2 sll
  //   $t4, $t1, 1 sw $t4, 14($zero)  # srl, word address 15 = 1 srl $t4, $t4, 1 sw $t4, 15($zero)  # sra,
  //   word address 16 = 256 sra $t4, $t1, 1 sw $t4, 16($zero)  # beq, $t5 = 1 beq $zero, $zero, branch
  //   addiu $t5, $zero, 1 branch: addiu $t5, $zero, 1  # bne, $t6 = 2 bne $zero, $zero, branch addiu $t6,
  //   $zero, 1 branch: addiu $t6, $zero, 1   # j, $t7 = 1  addu $t7, $t7, $zero j jump addiu $t7, $t7, 1
  //   jump: addiu $t7, $t7, 1  # jr, jal jump: addiu $t8, $zero, 1 jr $31 main: jal jump
  //   contents of ALUcontrol (hex, n*v repeats v):
  //   0 0 4 5 28*0 2 2 6 6 8 a c f b 9
endmodule
