// Logisim project MIPS_single_cycle.circ as structural Verilog: 4 circuits, main circuit main
module main (
);

  wire alu_1_bctrl, and_1_out, button_1_out, button_2_out, Clk_out, comparator_1_eq, comparator_2_eq,
       not_1_out;
  wire [3:0] ALUcontrol_data;
  wire [4:0] multiplexer_2_out, multiplexer_3_out;
  wire [5:0] selcontrol_1_out_4;
  wire [11:0] ControlUnit_data;
  wire [23:0] alu_1_rst;
  wire [31:0] adder_1_out, adder_2_out, bit_extender_1_out, connectbits_1_out_3, mips_ram_1_p7,
       mipsprogramrom_1_p2, multiplexer_1_out, multiplexer_4_out, multiplexer_5_out, multiplexer_6_out,
       multiplexer_7_out, PC_q, registerfile_1_p1, registerfile_1_p7, registerfile_1_p8, shifter_1_out;
  wire [31:24] alu_1_rst_2;

  Clock Clk (.out(Clk_out));
  ROM #(.addrWidth(6), .dataWidth(12)) ControlUnit (.addr(mipsprogramrom_1_p2[31:26]), .data(ControlUnit_data));
  Register #(.width(32)) PC (.D(multiplexer_6_out), .en(1'b1), .clk(Clk_out), .Q(PC_q), .clr(button_1_out));
  Button button_1 (.out(button_1_out));
  Adder #(.width(32)) adder_1 (.a(32'h4), .b(PC_q), .out(adder_1_out));  // open: cin, cout
  // MIPSProgramROM mipsprogramrom_1: pin names not known; wires that end beside it: PC_q, mipsprogramrom_1_p2, mipsprogramrom_1_p2[25:0]
  Adder #(.width(32)) adder_2 (.a(adder_1_out), .b(shifter_1_out), .out(adder_2_out));  // open: cin, cout
  and and_1 (and_1_out, ControlUnit_data[5], alu_1_bctrl);
  Multiplexer #(.width(32), .enable("false")) multiplexer_1 (
    .in0(adder_1_out), .in1(adder_2_out), .out(multiplexer_1_out), .sel(and_1_out));
  Multiplexer #(.width(5), .enable("false")) multiplexer_2 (
    .in0(multiplexer_3_out), .in1({5{1'b1}}), .out(multiplexer_2_out), .sel(ControlUnit_data[4]));
  Multiplexer #(.width(5), .enable("false")) multiplexer_3 (
    .in0(mipsprogramrom_1_p2[20:16]), .in1(mipsprogramrom_1_p2[15:11]), .out(multiplexer_3_out),
    .sel(ControlUnit_data[11]));
  ConnectBits connectbits_1 (.in_1(mipsprogramrom_1_p2[25:0]), .in_2(adder_1_out[31:28]), .out_3(connectbits_1_out_3));
  // RegisterFile registerfile_1: pin names not known; wires that end beside it: registerfile_1_p1, Clk_out, ControlUnit_data[8], multiplexer_2_out, mipsprogramrom_1_p2[25:21], mipsprogramrom_1_p2[20:16], registerfile_1_p7, registerfile_1_p8
  Multiplexer #(.width(32), .enable("false")) multiplexer_4 (
    .in0(registerfile_1_p8), .in1(bit_extender_1_out), .out(multiplexer_4_out), .sel(ControlUnit_data[10]));
  assign bit_extender_1_out = {{16{mipsprogramrom_1_p2[15]}}, mipsprogramrom_1_p2[15:0]};  // Bit_Extender bit_extender_1
  not not_1 (not_1_out, comparator_1_eq);
  Multiplexer #(.width(32), .enable("false")) multiplexer_5 (
    .in0(multiplexer_1_out), .in1(connectbits_1_out_3), .out(multiplexer_5_out), .sel(ControlUnit_data[4]));
  Shifter #(.width(32)) shifter_1 (.in(bit_extender_1_out), .\dist (5'b00010), .out(shifter_1_out));
  Multiplexer #(.width(32), .enable("false")) multiplexer_6 (
    .in0(registerfile_1_p7), .in1(multiplexer_5_out), .out(multiplexer_6_out), .sel(not_1_out));
  ALU alu_1 (
    .BNeEq(ControlUnit_data[9]), .A(registerfile_1_p7), .B(multiplexer_4_out), .OP(ALUcontrol_data),
    .SA(mipsprogramrom_1_p2[10:6]), .SltOP(comparator_2_eq), .BCtrl(alu_1_bctrl),
    .Rst({alu_1_rst_2, alu_1_rst}));
  SelControl selcontrol_1 (
    .FuncField(mipsprogramrom_1_p2[5:0]), .ALUop(ControlUnit_data[3:0]),
    .BitsChk(mipsprogramrom_1_p2[31:26]), .out_4(selcontrol_1_out_4));
  ROM #(.addrWidth(6), .dataWidth(4)) ALUcontrol (.addr(selcontrol_1_out_4), .data(ALUcontrol_data));
  Button button_2 (.out(button_2_out));
  Comparator #(.width(4), .mode("unsigned")) comparator_1 (
    .a(4'b1011), .b(ALUcontrol_data), .eq(comparator_1_eq));  // open: gt, lt
  Comparator #(.width(4), .mode("unsigned")) comparator_2 (
    .a(4'b1111), .b(ALUcontrol_data), .eq(comparator_2_eq));  // open: gt, lt
  Multiplexer #(.width(32), .enable("false")) multiplexer_7 (
    .in0({alu_1_rst_2, alu_1_rst}), .in1(mips_ram_1_p7), .out(multiplexer_7_out), .sel(ControlUnit_data[9]));
  // MIPS_RAM #(.addrWidth(24)) mips_ram_1: pin names not known; wires that end beside it: alu_1_rst, registerfile_1_p8, ControlUnit_data[6], Clk_out, ControlUnit_data[7], button_2_out, mips_ram_1_p7
  Multiplexer #(.width(32), .enable("false")) multiplexer_8 (
    .in0(multiplexer_7_out), .in1(adder_1_out), .out(registerfile_1_p1), .sel(ControlUnit_data[4]));

  // Notes on the sheet:
  //   0-3 ALUOP
  //   4 Jump
  //   5 Branch
  //   6 MemWrite
  //   7 MemRead
  //   8 RegWrite
  //   9 MemtoReg
  //   10 ALUSrc
  //   11 RegDst
  //   contents of ControlUnit (hex, n*v repeats v):
  //   900 0 10 110 220 20 0 0 0 501 50a 50b 504 505 506 20*0 781 7*0 441
  //   contents of mipsprogramrom_1 (hex, n*v repeats v):
  //   #init   addu $sp, $zero, $zero  addu $ra, $zero, $zero          addiu $sp, $sp, -4 #for n argument
  //   #you can change this line to whatever you want  addiu $t0, $zero, 5     sw $t0, 0($sp)          jal
  //   hailstone   addiu $t0, $zero, 1     j EXIT # hailstone(int n) need one argument hailstone:  addiu
  //   $sp, $sp, -8      sw $ra, 4($sp) #store add address of$ra         sw $fp, 0($sp) #store address of
  //   $fp    addu $fp, $sp, $zero    lw $s0, 8($fp) #load argument n         addiu $s1, $zero, 1 # 1
  //   #if n==1 return 0       beq $s0, $s1, R_zero    #n%2 = n&(2-1) = n&1    andi $s2, $s0, 1        #if
  //   (n%2) == 0  beq $s2, $zero, R_1     #else R_2:      #load next function     #we need to assign new
  //   n/2      addiu $sp, $sp, -4      #we know $s0 is n and we need to make n+1       addu $s4, $s0, $s0
  //   #n*2         addu $s4, $s4, $s0 #n*2+n = 3*n         addiu $s4, $s4, 1 #n+1  sw $s4, 0($sp) #store
  //   augment   jal hailstone #recursive        #when it out    #we don't need n anymore and don't need to
  //   load for use         addiu $sp, $sp, 4       lw $ra, 4($sp)  lw $fp, 0($sp)          addiu $sp, $sp,
  //   8       addiu $a0, $a0, 1 #return 1+recusive    jr $ra R_zero:          lw $ra, 4($sp)  lw $fp,
  //   0($sp)  addiu $sp, $sp, 8       #we will use a0 to return this function         addiu $a0, $a0, 0
  //   #return 0     jr $ra  R_1:    #load next function     #we need to assign new n/2      addiu $sp,
  //   $sp, -4      #we know $s0 is n and we need to make n/2 use SRA       sra $s3, $s0, 1 #n/2    sw $s3,
  //   0($sp) #store augment   jal hailstone #recursive        #when it out    #we don't need n anymore and
  //   don't need to load for use         addiu $sp, $sp, 4       lw $ra, 4($sp)  lw $fp, 0($sp)
  //   addiu $sp, $sp, 8       addiu $a0, $a0, 1 #return 1+recursive   jr $ra EXIT:    #just exit we must
  //   use syscall  #but it can't   #we will just move a0 to t0     addu $t0, $a0, $zero
  //   contents of ALUcontrol (hex, n*v repeats v):
  //   1 0 4 5 4*0 b 23*0 2 2 6 6 8 a c f 0 0 f f
endmodule

module ConnectBits (
  input  [25:0] in_1,
  input  [3:0] in_2,
  output [31:0] out_3
);

  wire [31:0] bit_extender_1_out, bit_extender_2_out, shifter_1_out, shifter_2_out;

  assign bit_extender_1_out = {{28{1'b0}}, in_2};  // Bit_Extender bit_extender_1
  assign bit_extender_2_out = {{6{1'b0}}, in_1};  // Bit_Extender bit_extender_2
  Shifter #(.width(32)) shifter_1 (.in(bit_extender_1_out), .\dist (5'b11100), .out(shifter_1_out));
  Shifter #(.width(32)) shifter_2 (.in(bit_extender_2_out), .\dist (5'b00010), .out(shifter_2_out));
  Adder #(.width(32)) adder_1 (.a(shifter_2_out), .b(shifter_1_out), .out(out_3));  // open: cin, cout
endmodule

module SelControl (
  input  [5:0] FuncField,
  input  [3:0] ALUop,
  input  [5:0] BitsChk,
  output [5:0] out_4
);

  wire comparator_1_eq, not_1_out;
  wire [5:0] adder_1_out, bit_extender_1_out;

  Adder #(.width(6)) adder_1 (.a(6'b100000), .b(bit_extender_1_out), .out(adder_1_out));  // open: cin, cout
  assign bit_extender_1_out = {{2{1'b0}}, ALUop};  // Bit_Extender bit_extender_1
  Multiplexer #(.width(6), .enable("false")) multiplexer_1 (
    .in0(FuncField), .in1(adder_1_out), .out(out_4), .sel(not_1_out));
  not not_1 (not_1_out, comparator_1_eq);
  Comparator #(.width(6), .mode("unsigned")) comparator_1 (
    .a(BitsChk), .b({6{1'b0}}), .eq(comparator_1_eq));  // open: gt, lt
endmodule

module ALU (
  input  BNeEq,
  input  [31:0] A,
  input  [31:0] B,
  input  [3:0] OP,
  input  [4:0] SA,
  input  SltOP,
  output BCtrl,
  output [31:0] Rst
);

  wire comparator_1_eq, comparator_1_lt, not_1_out;
  wire [31:0] bit_extender_1_out, mips_alu_1_p5;

  Multiplexer #(.enable("false")) multiplexer_1 (.in0(not_1_out), .in1(comparator_1_eq), .out(BCtrl), .sel(BNeEq));
  not not_1 (not_1_out, comparator_1_eq);
  Comparator #(.width(32)) comparator_1 (.a(A), .b(B), .eq(comparator_1_eq), .lt(comparator_1_lt));  // open: gt
  assign bit_extender_1_out = {{31{1'b0}}, comparator_1_lt};  // Bit_Extender bit_extender_1
  // Mips_ALU mips_alu_1: pin names not known; wires that end beside it: A, B, OP, SA, mips_alu_1_p5
  Multiplexer #(.width(32), .enable("false")) multiplexer_2 (
    .in0(mips_alu_1_p5), .in1(bit_extender_1_out), .out(Rst), .sel(SltOP));
endmodule
