// Logisim project MIPS_add.circ as structural Verilog: 1 circuit, main circuit main
module main (
);

  wire Clk_out, registerfile_1_p1, registerfile_1_p6;
  wire [1:0] ControlUnit_data;
  wire [3:0] ALUcontrol_data;
  wire [4:0] multiplexer_1_out;
  wire [5:0] mipsprogramrom_1_p2_2;
  wire [25:0] mipsprogramrom_1_p2;
  wire [31:0] adder_1_out, bit_extender_1_out, multiplexer_2_out, PC_q, registerfile_1_p7;

  Clock Clk (.out(Clk_out));
  Register #(.width(32)) PC (.D(adder_1_out), .en(1'b1), .clk(Clk_out), .Q(PC_q));  // open: clr
  ROM #(.addrWidth(6), .dataWidth(2)) ControlUnit (.addr(mipsprogramrom_1_p2_2), .data(ControlUnit_data));
  Adder #(.width(32)) adder_1 (.a(32'h4), .b(PC_q), .out(adder_1_out));  // open: cin, cout
  // MIPSProgramROM mipsprogramrom_1: pin names not known; wires that end beside it: PC_q, {mipsprogramrom_1_p2_2, mipsprogramrom_1_p2}, Clk_out
  Multiplexer #(.width(5), .enable("false")) multiplexer_1 (
    .in0(mipsprogramrom_1_p2[20:16]), .in1(mipsprogramrom_1_p2[15:11]), .out(multiplexer_1_out),
    .sel(ControlUnit_data[1]));
  ROM #(.addrWidth(6), .dataWidth(4)) ALUcontrol (.addr(mipsprogramrom_1_p2[5:0]), .data(ALUcontrol_data));
  // RegisterFile registerfile_1: pin names not known; wires that end beside it: registerfile_1_p1, 1'b1, multiplexer_1_out, mipsprogramrom_1_p2[25:21], mipsprogramrom_1_p2[20:16], registerfile_1_p6, registerfile_1_p7
  assign bit_extender_1_out = {{16{mipsprogramrom_1_p2[15]}}, mipsprogramrom_1_p2[15:0]};  // Bit_Extender bit_extender_1
  Multiplexer #(.width(32), .enable("false")) multiplexer_2 (
    .in0(registerfile_1_p7), .in1(bit_extender_1_out), .out(multiplexer_2_out), .sel(ControlUnit_data[0]));
  // Mips_ALU mips_alu_1: pin names not known; wires that end beside it: registerfile_1_p6, multiplexer_2_out, ALUcontrol_data, registerfile_1_p1

  // Notes on the sheet:
  //   contents of ControlUnit (hex, n*v repeats v):
  //   2 7*0 1 1
  //   contents of mipsprogramrom_1 (hex, n*v repeats v):
  //   addiu $t1, $zero, 2 addu $t2, $t0, $t1
  //   contents of ALUcontrol (hex, n*v repeats v):
  //   0 2 2 29*0 2 2
endmodule
