// Logisim project MIPS_single_cycle.circ as structural Verilog: 2 circuits, main circuit main
module main (
);

  wire and_1_out, and_2_out, button_1_out, Clk_out, comparator_1_eq;
  wire [3:0] adder_1_out_2, mips_alu_1_p3;
  wire [4:0] multiplexer_2_out, multiplexer_3_out;
  wire [5:0] adder_2_out, bit_extender_2_out, mipsprogramrom_1_p2_2, multiplexer_6_out;
  wire [10:0] ControlUnit_data;
  wire [23:0] mips_alu_1_p4;
  wire [25:0] mipsprogramrom_1_p2, shifter_1_out;
  wire [27:0] adder_1_out;
  wire [31:0] adder_3_out, bit_extender_1_out, connectbits_1_out_3, mips_ram_1_p5, multiplexer_1_out,
       multiplexer_4_out, multiplexer_5_out, multiplexer_7_out, PC_q, registerfile_1_p1, registerfile_1_p7,
       registerfile_1_p8, shifter_2_out;
  wire [31:24] mips_alu_1_p4_2;

  Clock Clk (.out(Clk_out));
  ROM #(.addrWidth(6), .dataWidth(11)) ControlUnit (.addr(mipsprogramrom_1_p2_2), .data(ControlUnit_data));
  Register #(.width(32)) PC (.D(multiplexer_5_out), .en(1'b1), .clk(Clk_out), .Q(PC_q), .clr(button_1_out));
  Button button_1 (.out(button_1_out));
  Adder #(.width(32)) adder_1 (.a(32'h4), .b(PC_q), .out({adder_1_out_2, adder_1_out}));  // open: cin, cout
  Multiplexer #(.width(32), .enable("false")) multiplexer_1 (
    .in0({adder_1_out_2, adder_1_out}), .in1(shifter_2_out), .out(multiplexer_1_out), .sel(and_1_out));
  and and_1 (and_1_out, ControlUnit_data[4], comparator_1_eq);
  // MIPSProgramROM mipsprogramrom_1: pin names not known; wires that end beside it: PC_q, {mipsprogramrom_1_p2_2, mipsprogramrom_1_p2}, adder_1_out_2
  Multiplexer #(.width(5), .enable("false")) multiplexer_2 (
    .in0(multiplexer_3_out), .in1({5{1'b1}}), .out(multiplexer_2_out), .sel(ControlUnit_data[3]));
  Multiplexer #(.width(5), .enable("false")) multiplexer_3 (
    .in0(mipsprogramrom_1_p2[20:16]), .in1(mipsprogramrom_1_p2[15:11]), .out(multiplexer_3_out),
    .sel(ControlUnit_data[10]));
  Shifter #(.width(26)) shifter_1 (.in(mipsprogramrom_1_p2), .\dist (5'b00010), .out(shifter_1_out));
  Comparator #(.width(32)) comparator_1 (
    .a(registerfile_1_p7), .b(registerfile_1_p8), .eq(comparator_1_eq));  // open: gt, lt
  // RegisterFile registerfile_1: pin names not known; wires that end beside it: registerfile_1_p1, Clk_out, ControlUnit_data[7], multiplexer_2_out, mipsprogramrom_1_p2[25:21], mipsprogramrom_1_p2[20:16], registerfile_1_p7, registerfile_1_p8
  assign bit_extender_1_out = {{16{mipsprogramrom_1_p2[15]}}, mipsprogramrom_1_p2[15:0]};  // Bit_Extender bit_extender_1
  assign bit_extender_2_out = {{3{1'b0}}, ControlUnit_data[2:0]};  // Bit_Extender bit_extender_2
  connectBits connectbits_1 (.in_1(shifter_1_out), .in_2(adder_1_out_2), .out_3(connectbits_1_out_3));
  Multiplexer #(.width(32), .enable("false")) multiplexer_4 (
    .in0(registerfile_1_p8), .in1(bit_extender_1_out), .out(multiplexer_4_out), .sel(ControlUnit_data[9]));
  Shifter #(.width(32)) shifter_2 (.in(bit_extender_1_out), .\dist (5'b00010), .out(shifter_2_out));
  Adder #(.width(6)) adder_2 (.a(6'b100000), .b(bit_extender_2_out), .out(adder_2_out));  // open: cin, cout
  and and_2 (and_2_out, mipsprogramrom_1_p2_2[0], 1'b1);
  Multiplexer #(.width(32), .enable("false")) multiplexer_5 (
    .in0(multiplexer_1_out), .in1(connectbits_1_out_3), .out(multiplexer_5_out), .sel(ControlUnit_data[3]));
  // Mips_ALU mips_alu_1: pin names not known; wires that end beside it: registerfile_1_p7, multiplexer_4_out, mips_alu_1_p3, {mips_alu_1_p4_2, mips_alu_1_p4}, registerfile_1_p8
  ROM #(.addrWidth(6), .dataWidth(4)) ALUcontrol (.addr(multiplexer_6_out), .data(mips_alu_1_p3));
  Multiplexer #(.width(6), .enable("false")) multiplexer_6 (
    .in0(mipsprogramrom_1_p2[5:0]), .in1(adder_2_out), .out(multiplexer_6_out), .sel(and_2_out));
  Multiplexer #(.width(32), .enable("false")) multiplexer_7 (
    .in0({mips_alu_1_p4_2, mips_alu_1_p4}), .in1(mips_ram_1_p5), .out(multiplexer_7_out),
    .sel(ControlUnit_data[8]));
  // MIPS_RAM #(.addrWidth(24)) mips_ram_1: pin names not known; wires that end beside it: mips_alu_1_p4, ControlUnit_data[5], Clk_out, ControlUnit_data[6], mips_ram_1_p5
  Multiplexer #(.width(32), .enable("false")) multiplexer_8 (
    .in0(multiplexer_7_out), .in1(adder_3_out), .out(registerfile_1_p1), .sel(ControlUnit_data[3]));
  Adder #(.width(32)) adder_3 (.a(32'h4), .b({adder_1_out_2, adder_1_out}), .out(adder_3_out));  // open: cin, cout

  // Notes on the sheet:
  //   contents of ControlUnit (hex, n*v repeats v):
  //   482 0 8 88 17 18 0 0 280 281 0 0 284 285 286 20*0 3c0 7*0 220
  //   contents of mipsprogramrom_1 (hex, n*v repeats v):
  //   jal jump addiu $t9, $zero, 2 j exit jump: addiu $t8, $zero, 1 jr $31 exit:
  //   contents of ALUcontrol (hex, n*v repeats v):
  //   0 0 4 5 28*0 2 2 6 6 8 a c f b 9
  //   pc+4
endmodule

module connectBits (
  input  [25:0] in_1,
  input  [3:0] in_2,
  output [31:0] out_3
);

  wire [31:0] bit_extender_1_out, bit_extender_2_out, shifter_1_out;

  assign bit_extender_1_out = {{28{1'b0}}, in_2};  // Bit_Extender bit_extender_1
  assign bit_extender_2_out = {{6{1'b0}}, in_1};  // Bit_Extender bit_extender_2
  Shifter #(.width(32)) shifter_1 (.in(bit_extender_1_out), .\dist (5'b11100), .out(shifter_1_out));
  Adder #(.width(32)) adder_1 (.a(bit_extender_2_out), .b(shifter_1_out), .out(out_3));  // open: cin, cout
endmodule
