// Logisim project mips_pipeline.circ as structural Verilog: 16 circuits, main circuit main
module main (
  output [15:0] out_1
);

  wire Clk_out, exe_mem_1_sjumpr, exe_mem_1_smemread, exe_mem_1_smemtoreg, exe_mem_1_smemwrite,
       exe_mem_1_sregwrite, execute_1_jal, execute_1_pcsrc, execute_1_sjump, execute_1_smemread,
       execute_1_smemtoreg, execute_1_smemwrite, execute_1_sregwrite, id_exe_1_salusrc, id_exe_1_sbranch,
       id_exe_1_sjump, id_exe_1_smemread, id_exe_1_smemtoreg, id_exe_1_smemwrite, id_exe_1_sregdst,
       id_exe_1_sregwrite, instructiondecode_1_salusrc, instructiondecode_1_sbranch,
       instructiondecode_1_sjump, instructiondecode_1_smemread, instructiondecode_1_smemtoreg,
       instructiondecode_1_smemwrite, instructiondecode_1_sregdst, instructiondecode_1_sregwrite,
       mem_1_sjumpr, mem_1_smemtoreg, mem_1_sregwrite, mem_wb_1_sjumpr, mem_wb_1_smemtoreg,
       mem_wb_1_sregwrite, wb_1_sregwrite;
  wire [3:0] id_exe_1_saluop, instructiondecode_1_saluop;
  wire [4:0] exe_mem_1_sregsel, exe_mem_1_srwrite, execute_1_rwrite, execute_1_sregsel, mem_1_sregsel,
       mem_1_srwrite, mem_wb_1_sregsel, mem_wb_1_srwrite, wb_1_sregsel, wb_1_srwrite;
  wire [31:0] exe_mem_1_saddrs, exe_mem_1_sdwrite, exe_mem_1_spc4, execute_1_baddrs, execute_1_dwrite,
       execute_1_jaddrs, execute_1_r31, execute_1_rst, execute_1_spc4, id_exe_1_sa, id_exe_1_sb,
       id_exe_1_scode, id_exe_1_simmediate, id_exe_1_spc4, if_id_1_sopcode, if_id_1_spc4,
       instructiondecode_1_a, instructiondecode_1_b, instructiondecode_1_immediate,
       instructiondecode_1_scode, instructiondecode_1_spc4, instructionfetch_1_code, instructionfetch_1_pc4,
       mem_1_sdatar, mem_1_spc4, mem_1_srst, mem_wb_1_sdatar, mem_wb_1_spc4, mem_wb_1_srst, wb_1_datawb;

  Clock Clk (.out(Clk_out));
  count count_1 (.in_1(Clk_out), .out_2(out_1));
  InstructionFetch instructionfetch_1 (
    .Clk(Clk_out), .pcsrc(execute_1_pcsrc), .jump(execute_1_sjump), .jal(execute_1_jal),
    .BAddrs(execute_1_baddrs), .JAddrs(execute_1_jaddrs), .R31(execute_1_r31),
    .Code(instructionfetch_1_code), .PC4(instructionfetch_1_pc4));
  IF_ID if_id_1 (
    .SPC4(if_id_1_spc4), .Clk(Clk_out), .SOPCode(if_id_1_sopcode), .OPCode(instructionfetch_1_code),
    .PC4(instructionfetch_1_pc4));
  InstructionDecode instructiondecode_1 (
    .Clk(Clk_out), .regwrite(wb_1_sregwrite), .DWrite(wb_1_datawb), .RWrite(wb_1_srwrite),
    .Code(if_id_1_sopcode), .PC4(if_id_1_spc4), .Sregwrite(instructiondecode_1_sregwrite),
    .Smemwrite(instructiondecode_1_smemwrite), .Smemread(instructiondecode_1_smemread),
    .SALUOp(instructiondecode_1_saluop), .Sjump(instructiondecode_1_sjump),
    .Sbranch(instructiondecode_1_sbranch), .Smemtoreg(instructiondecode_1_smemtoreg),
    .Salusrc(instructiondecode_1_salusrc), .Sregdst(instructiondecode_1_sregdst), .A(instructiondecode_1_a),
    .B(instructiondecode_1_b), .Immediate(instructiondecode_1_immediate), .SCode(instructiondecode_1_scode),
    .SPC4(instructiondecode_1_spc4));
  ID_EXE id_exe_1 (
    .Clk(Clk_out), .regwrite(instructiondecode_1_sregwrite), .memwrite(instructiondecode_1_smemwrite),
    .memread(instructiondecode_1_smemread), .ALUOp(instructiondecode_1_saluop),
    .jump(instructiondecode_1_sjump), .branch(instructiondecode_1_sbranch),
    .momtoreg(instructiondecode_1_smemtoreg), .alusrc(instructiondecode_1_salusrc),
    .regdst(instructiondecode_1_sregdst), .A(instructiondecode_1_a), .B(instructiondecode_1_b),
    .Immediate(instructiondecode_1_immediate), .Code(instructiondecode_1_scode),
    .PC4(instructiondecode_1_spc4), .Sregwrite(id_exe_1_sregwrite), .Smemwrite(id_exe_1_smemwrite),
    .Smemread(id_exe_1_smemread), .SALUop(id_exe_1_saluop), .Sjump(id_exe_1_sjump),
    .Sbranch(id_exe_1_sbranch), .Smemtoreg(id_exe_1_smemtoreg), .Salusrc(id_exe_1_salusrc),
    .Sregdst(id_exe_1_sregdst), .SA(id_exe_1_sa), .SB(id_exe_1_sb), .SImmediate(id_exe_1_simmediate),
    .SCode(id_exe_1_scode), .SPC4(id_exe_1_spc4));
  Execute execute_1 (
    .regwrite(id_exe_1_sregwrite), .memwrite(id_exe_1_smemwrite), .memread(id_exe_1_smemread),
    .ALUOp(id_exe_1_saluop), .jump(id_exe_1_sjump), .branch(id_exe_1_sbranch), .memtoreg(id_exe_1_smemtoreg),
    .alusrc(id_exe_1_salusrc), .regdst(id_exe_1_sregdst), .A(id_exe_1_sa), .B(id_exe_1_sb),
    .Immediate(id_exe_1_simmediate), .Code(id_exe_1_scode), .PC4(id_exe_1_spc4), .RstWb(wb_1_datawb),
    .RstExe(mem_1_srst), .RdExeMem(mem_1_sregsel), .RdMemWb(wb_1_sregsel), .RWMemWb(wb_1_sregwrite),
    .RWExMem(mem_1_sregwrite), .Sregwrite(execute_1_sregwrite), .Sjump(execute_1_sjump),
    .Smemtoreg(execute_1_smemtoreg), .Smemwrite(execute_1_smemwrite), .Smemread(execute_1_smemread),
    .pcsrc(execute_1_pcsrc), .Rst(execute_1_rst), .DWrite(execute_1_dwrite), .jal(execute_1_jal),
    .BAddrs(execute_1_baddrs), .JAddrs(execute_1_jaddrs), .R31(execute_1_r31), .RWrite(execute_1_rwrite),
    .SPC4(execute_1_spc4), .SRegSel(execute_1_sregsel));
  EXE_MEM exe_mem_1 (
    .Clk(Clk_out), .regwrite(execute_1_sregwrite), .jumpR(execute_1_sjump), .memtoreg(execute_1_smemtoreg),
    .memwrite(execute_1_smemwrite), .memread(execute_1_smemread), .Addrs(execute_1_rst),
    .DWrite(execute_1_dwrite), .RWrite(execute_1_rwrite), .PC4(execute_1_spc4), .RegSel(execute_1_sregsel),
    .Sregwrite(exe_mem_1_sregwrite), .SjumpR(exe_mem_1_sjumpr), .Smemtoreg(exe_mem_1_smemtoreg),
    .Smemwrite(exe_mem_1_smemwrite), .Smemread(exe_mem_1_smemread), .SAddrs(exe_mem_1_saddrs),
    .SDWrite(exe_mem_1_sdwrite), .SRWrite(exe_mem_1_srwrite), .SPC4(exe_mem_1_spc4),
    .SRegSel(exe_mem_1_sregsel));
  Mem mem_1 (
    .Clk(Clk_out), .regwrite(exe_mem_1_sregwrite), .jumpR(exe_mem_1_sjumpr), .memtoreg(exe_mem_1_smemtoreg),
    .memwrite(exe_mem_1_smemwrite), .memread(exe_mem_1_smemread), .Addrs(exe_mem_1_saddrs),
    .DWrite(exe_mem_1_sdwrite), .RWrite(exe_mem_1_srwrite), .PC4(exe_mem_1_spc4), .RegSel(exe_mem_1_sregsel),
    .Sregwrite(mem_1_sregwrite), .SjumpR(mem_1_sjumpr), .Smemtoreg(mem_1_smemtoreg), .SDataR(mem_1_sdatar),
    .SRst(mem_1_srst), .SRWrite(mem_1_srwrite), .SPC4(mem_1_spc4), .SRegSel(mem_1_sregsel));
  MEM_WB mem_wb_1 (
    .Clk(Clk_out), .regwrite(mem_1_sregwrite), .jumpR(mem_1_sjumpr), .memtoreg(mem_1_smemtoreg),
    .DataR(mem_1_sdatar), .Rst(mem_1_srst), .RWrite(mem_1_srwrite), .PC4(mem_1_spc4), .RegSel(mem_1_sregsel),
    .Sregwrite(mem_wb_1_sregwrite), .SjumpR(mem_wb_1_sjumpr), .Smemtoreg(mem_wb_1_smemtoreg),
    .SDataR(mem_wb_1_sdatar), .SRst(mem_wb_1_srst), .SRWrite(mem_wb_1_srwrite), .SPC4(mem_wb_1_spc4),
    .SRegSel(mem_wb_1_sregsel));
  WB wb_1 (
    .regwrite(mem_wb_1_sregwrite), .jumpR(mem_wb_1_sjumpr), .memtoreg(mem_wb_1_smemtoreg),
    .DataRead(mem_wb_1_sdatar), .Rst(mem_wb_1_srst), .RWrite(mem_wb_1_srwrite), .PC4(mem_wb_1_spc4),
    .RegSel(mem_wb_1_sregsel), .Sregwrite(wb_1_sregwrite), .DataWB(wb_1_datawb), .SRWrite(wb_1_srwrite),
    .SRegSel(wb_1_sregsel));
endmodule

module ConnectBits (
  input  [25:0] in_1,
  input  [3:0] in_2,
  output [31:0] out_3
);

  wire [31:0] bit_extender_1_out, bit_extender_2_out, shifter_1_out, shifter_2_out;

  assign bit_extender_1_out = {{28{1'b0}}, in_2};  // Bit_Extender bit_extender_1
  assign bit_extender_2_out = {{6{1'b0}}, in_1};  // Bit_Extender bit_extender_2
  Shifter #(.width(32)) shifter_1 (.in(bit_extender_1_out), .\dist (5'b11100), .out(shifter_1_out));
  Shifter #(.width(32)) shifter_2 (.in(bit_extender_2_out), .\dist (5'b00010), .out(shifter_2_out));
  Adder #(.width(32)) adder_1 (.a(shifter_2_out), .b(shifter_1_out), .out(out_3));  // open: cin, cout
endmodule

module SelControl (
  input  [5:0] FuncField,
  input  [3:0] ALUop,
  input  [5:0] BitsChk,
  output [5:0] out_4
);

  wire comparator_1_eq, not_1_out;
  wire [5:0] adder_1_out, bit_extender_1_out;

  Adder #(.width(6)) adder_1 (.a(6'b100000), .b(bit_extender_1_out), .out(adder_1_out));  // open: cin, cout
  assign bit_extender_1_out = {{2{1'b0}}, ALUop};  // Bit_Extender bit_extender_1
  Multiplexer #(.width(6), .enable("false")) multiplexer_1 (
    .in0(FuncField), .in1(adder_1_out), .out(out_4), .sel(not_1_out));
  not not_1 (not_1_out, comparator_1_eq);
  Comparator #(.width(6), .mode("unsigned")) comparator_1 (
    .a(BitsChk), .b({6{1'b0}}), .eq(comparator_1_eq));  // open: gt, lt
endmodule

module ALU (
  input  BNeEq,
  input  [31:0] A,
  input  [31:0] B,
  input  [3:0] OP,
  input  [4:0] SA,
  input  SltOP,
  output BCtrl,
  output [31:0] Rst
);

  wire comparator_1_eq, comparator_1_lt, not_1_out;
  wire [31:0] bit_extender_1_out, mips_alu_1_p5;

  Multiplexer #(.enable("false")) multiplexer_1 (.in0(not_1_out), .in1(comparator_1_eq), .out(BCtrl), .sel(BNeEq));
  not not_1 (not_1_out, comparator_1_eq);
  Comparator #(.width(32)) comparator_1 (.a(A), .b(B), .eq(comparator_1_eq), .lt(comparator_1_lt));  // open: gt
  assign bit_extender_1_out = {{31{1'b0}}, comparator_1_lt};  // Bit_Extender bit_extender_1
  // Mips_ALU mips_alu_1: pin names not known; wires that end beside it: A, B, OP, SA, mips_alu_1_p5
  Multiplexer #(.width(32), .enable("false")) multiplexer_2 (
    .in0(mips_alu_1_p5), .in1(bit_extender_1_out), .out(Rst), .sel(SltOP));
endmodule

module WB (
  input  regwrite,
  input  jumpR,
  input  memtoreg,
  input  [31:0] DataRead,
  input  [31:0] Rst,
  input  [4:0] RWrite,
  input  [31:0] PC4,
  input  [4:0] RegSel,
  output Sregwrite,
  output [31:0] DataWB,
  output [4:0] SRWrite,
  output [4:0] SRegSel
);

  wire [31:0] adder_1_out, multiplexer_1_out;

  Multiplexer #(.width(32), .enable("false")) multiplexer_1 (
    .in0(Rst), .in1(DataRead), .out(multiplexer_1_out), .sel(memtoreg));
  Adder #(.width(32)) adder_1 (.a(32'h4), .b(PC4), .out(adder_1_out));  // open: cin, cout
  Multiplexer #(.width(32), .enable("false")) multiplexer_2 (
    .in0(multiplexer_1_out), .in1(adder_1_out), .out(DataWB), .sel(jumpR));

  assign SRegSel = RegSel;
  assign Sregwrite = regwrite;
  assign SRWrite = RWrite;
endmodule

module Mem (
  input  Clk,
  input  regwrite,
  input  jumpR,
  input  memtoreg,
  input  memwrite,
  input  memread,
  input  [31:0] Addrs,
  input  [31:0] DWrite,
  input  [4:0] RWrite,
  input  [31:0] PC4,
  input  [4:0] RegSel,
  output Sregwrite,
  output SjumpR,
  output Smemtoreg,
  output [31:0] SDataR,
  output [31:0] SRst,
  output [4:0] SRWrite,
  output [31:0] SPC4,
  output [4:0] SRegSel
);

  wire button_1_out;

  Button button_1 (.out(button_1_out));
  // MIPS_RAM #(.addrWidth(24)) mips_ram_1: pin names not known; wires that end beside it: Addrs[23:0], DWrite, memwrite, Clk, memread, button_1_out, SDataR

  assign SjumpR = jumpR;
  assign Smemtoreg = memtoreg;
  assign SPC4 = PC4;
  assign SRegSel = RegSel;
  assign Sregwrite = regwrite;
  assign SRst = Addrs;
  assign SRWrite = RWrite;
endmodule

module InstructionFetch (
  input  Clk,
  input  pcsrc,
  input  jump,
  input  jal,
  input  [31:0] BAddrs,
  input  [31:0] JAddrs,
  input  [31:0] R31,
  output [31:0] Code,
  output [31:0] PC4
);

  wire button_1_out, not_1_out;
  wire [31:0] multiplexer_1_out, multiplexer_2_out, multiplexer_3_out, register_1_q;

  Register #(.width(32), .trigger("falling")) register_1 (
    .D(multiplexer_2_out), .en(1'b1), .clk(Clk), .Q(register_1_q), .clr(button_1_out));
  Button button_1 (.out(button_1_out));
  Adder #(.width(32)) adder_1 (.a(32'h4), .b(register_1_q), .out(PC4));  // open: cin, cout
  // MIPSProgramROM mipsprogramrom_1: pin names not known; wires that end beside it: register_1_q, Code
  Multiplexer #(.width(32), .enable("false")) multiplexer_1 (
    .in0(PC4), .in1(BAddrs), .out(multiplexer_1_out), .sel(pcsrc));
  not not_1 (not_1_out, jal);
  Multiplexer #(.width(32), .enable("false")) multiplexer_2 (
    .in0(R31), .in1(multiplexer_3_out), .out(multiplexer_2_out), .sel(not_1_out));
  Multiplexer #(.width(32), .enable("false")) multiplexer_3 (
    .in0(multiplexer_1_out), .in1(JAddrs), .out(multiplexer_3_out), .sel(jump));

  // Notes on the sheet:
  //   contents of mipsprogramrom_1 (hex, n*v repeats v):
  //   addu $s1, $zero, $zero                                  # 5     addu $s3, $zero, $zero
  //   # 6     addiu $sp, $sp, -4                                              # 7     addiu $s0, $0, 5
  //   # 8     jal HAILSTONE                                                   # 9     sw $s0, 0($sp)
  //   # 10    addiu $sp, $sp, 4                                               # 57    addu $s1, $s1, $v0
  //   # 58    addiu $sp, $sp, -12                                             # 59    sw $s1, 8($sp)
  //   # 60    addiu $s1, $s1, 1                                               # 61    sw $s1, 4($sp)
  //   # 62    addiu $s1, $s1, 1                                               # 63    sw $s1, 0($sp)
  //   # 64    lw $s2, 8($sp)                                                  # 65    addu $s3, $s2, $zero
  //   # 66    lw $s2, 4($sp)                                                  # 67    addu $s3, $s2, $s3
  //   # 68    lw $s2, 0($sp)                                                  # 69    addu $s3, $s2, $s3
  //   # 70    nop                                                                                     nop
  //   nop                                                                                     nop
  //   nop                                                                               HAILSTONE:
  //   addiu $sp, $sp, -8                                              # 11    sw $ra, 4($sp)
  //   # 12    sw $fp, 0($sp)                                                  # 13    addu $fp, $sp, $zero
  //   # 14    lw $t0, 8($fp)                                                  # 15    addiu $t1, $zero, 1
  //   # 16    addu $t2, $zero, $zero                                  # 17 WHILE:     beq $t0, $t1,
  //   WHILE_OUT                                 # 18, 26, 32, 38, 44, 50        andi $t3, $t0, 1
  //   # 19, 27, 33, 39, 45, 51 WHILE_IN:      bne $t3, $zero, ELSE                                    #
  //   20, 28, 34, 40, 46    addiu $t2, $t2, 1                                               # 21, 29, 35,
  //   41, 47 IF:        j WHILE                                                                 #     30,
  //   36, 42, 48    sra $t0, $t0, 1                                                 #     31, 37, 43, 49
  //   ELSE:     addu $t4, $t0, $t0                                              # 22    addu $t0, $t0, $t4
  //   # 23    j WHILE                                                                 # 24    addiu $t0,
  //   $t0, 1                                               # 25  WHILE_OUT:        lw $ra, 4($sp)
  //   # 52    lw $fp, 0($sp)                                                  # 53    addiu $sp, $sp, 8
  //   # 54    jr $ra                                                                  # 55    addu $v0,
  //   $t2, $zero                                    # 56
endmodule

module InstructionDecode (
  input  Clk,
  input  regwrite,
  input  [31:0] DWrite,
  input  [4:0] RWrite,
  input  [31:0] Code,
  input  [31:0] PC4,
  output Sregwrite,
  output Smemwrite,
  output Smemread,
  output [3:0] SALUOp,
  output Sjump,
  output Sbranch,
  output Smemtoreg,
  output Salusrc,
  output Sregdst,
  output [31:0] A,
  output [31:0] B,
  output [31:0] Immediate,
  output [31:0] SCode,
  output [31:0] SPC4
);

  ROM #(.addrWidth(6), .dataWidth(12)) rom_1 (
    .addr(Code[31:26]),
    .data({Sregdst, Salusrc, Smemtoreg, Sregwrite, Smemread, Smemwrite, Sbranch, Sjump, SALUOp}));
  // RegisterFile #(.trigger("falling")) registerfile_1: pin names not known; wires that end beside it: DWrite, Clk, regwrite, RWrite, Code[25:21], Code[20:16], A, B
  assign Immediate = {{16{Code[15]}}, Code[15:0]};  // Bit_Extender bit_extender_1

  assign SCode = Code;
  assign SPC4 = PC4;

  // Notes on the sheet:
  //   0-3 ALUOP
  //   4 Jump
  //   5 Branch
  //   6 MemWrite
  //   7 MemRead
  //   8 RegWrite
  //   9 MemtoReg
  //   10 ALUSrc
  //   11 RegDst
  //   contents of rom_1 (hex, n*v repeats v):
  //   900 0 10 110 220 20 0 0 0 501 50a 50b 504 505 506 20*0 781 7*0 441
endmodule

module Execute (
  input  regwrite,
  input  memwrite,
  input  memread,
  input  [3:0] ALUOp,
  input  jump,
  input  branch,
  input  memtoreg,
  input  alusrc,
  input  regdst,
  input  [31:0] A,
  input  [31:0] B,
  input  [31:0] Immediate,
  input  [31:0] Code,
  input  [31:0] PC4,
  input  [31:0] RstWb,
  input  [31:0] RstExe,
  input  [4:0] RdExeMem,
  input  [4:0] RdMemWb,
  input  RWMemWb,
  input  RWExMem,
  output Sregwrite,
  output Sjump,
  output Smemtoreg,
  output Smemwrite,
  output Smemread,
  output pcsrc,
  output [31:0] Rst,
  output [31:0] DWrite,
  output jal,
  output [31:0] BAddrs,
  output [31:0] JAddrs,
  output [31:0] R31,
  output [4:0] RWrite,
  output [31:0] SPC4,
  output [4:0] SRegSel
);

  wire alu_1_bctrl, comparator_2_eq;
  wire [1:0] RsSelect, RtSelect;
  wire [3:0] rom_1_data;
  wire [5:0] selcontrol_1_out_4;
  wire [31:0] multiplexer_3_out, shifter_1_out;

  Multiplexer #(.select(2), .width(32), .enable("false")) multiplexer_1 (
    .in0(A), .in1(RstExe), .in2(RstWb), .out(R31), .sel(RsSelect));  // open: in3
  Multiplexer #(.select(2), .width(32), .enable("false")) multiplexer_2 (
    .in0(B), .in1(RstExe), .in2(RstWb), .out(DWrite), .sel(RtSelect));  // open: in3
  Multiplexer #(.width(32), .enable("false")) multiplexer_3 (
    .in0(DWrite), .in1(Immediate), .out(multiplexer_3_out), .sel(alusrc));
  Shifter #(.width(32)) shifter_1 (.in(Immediate), .\dist (5'b00010), .out(shifter_1_out));
  Multiplexer #(.width(5), .enable("false")) multiplexer_4 (
    .in0(Code[20:16]), .in1(Code[15:11]), .out(SRegSel), .sel(regdst));
  Adder #(.width(32)) adder_1 (.a(shifter_1_out), .b(PC4), .out(BAddrs));  // open: cin, cout
  ConnectBits connectbits_1 (.in_1(Code[25:0]), .in_2(PC4[31:28]), .out_3(JAddrs));
  SelControl selcontrol_1 (.FuncField(Code[5:0]), .ALUop(ALUOp), .BitsChk(Code[31:26]), .out_4(selcontrol_1_out_4));
  Multiplexer #(.width(5), .enable("false")) multiplexer_5 (.in0(SRegSel), .in1({5{1'b1}}), .out(RWrite), .sel(jump));
  ROM #(.addrWidth(6), .dataWidth(4)) rom_1 (.addr(selcontrol_1_out_4), .data(rom_1_data));
  Forwarding forwarding_1 (
    .Rs(Code[25:21]), .Rt(Code[20:16]), .RdExMem(RdExeMem), .RdMemWb(RdMemWb), .RWExMem(RWExMem),
    .RWMemWb(RWMemWb), .RsSelector(RsSelect), .RtSelector(RtSelect));
  and and_1 (pcsrc, branch, alu_1_bctrl);
  ALU alu_1 (
    .BNeEq(memtoreg), .A(R31), .B(multiplexer_3_out), .OP(rom_1_data), .SA(Code[10:6]),
    .SltOP(comparator_2_eq), .BCtrl(alu_1_bctrl), .Rst(Rst));
  Comparator #(.width(4), .mode("unsigned")) comparator_1 (.a(4'b1011), .b(rom_1_data), .eq(jal));  // open: gt, lt
  Comparator #(.width(4), .mode("unsigned")) comparator_2 (
    .a(4'b1111), .b(rom_1_data), .eq(comparator_2_eq));  // open: gt, lt

  assign Sjump = jump;
  assign Smemread = memread;
  assign Smemtoreg = memtoreg;
  assign Smemwrite = memwrite;
  assign SPC4 = PC4;
  assign Sregwrite = regwrite;

  // Notes on the sheet:
  //   contents of rom_1 (hex, n*v repeats v):
  //   1 0 4 5 4*0 b 23*0 2 2 6 6 8 a c f 0 0 f f
endmodule

module IF_ID (
  input  Clk,
  input  [31:0] OPCode,
  input  [31:0] PC4,
  output [31:0] SOPCode,
  output [31:0] SPC4
);

  Register #(.width(32)) register_1 (.D(OPCode), .en(1'b1), .clk(Clk), .Q(SOPCode));  // open: clr
  Register #(.width(32)) register_2 (.D(PC4), .en(1'b1), .clk(Clk), .Q(SPC4));  // open: clr
endmodule

module ID_EXE (
  input  Clk,
  input  regwrite,
  input  memwrite,
  input  memread,
  input  [3:0] ALUOp,
  input  jump,
  input  branch,
  input  momtoreg,
  input  alusrc,
  input  regdst,
  input  [31:0] A,
  input  [31:0] B,
  input  [31:0] Immediate,
  input  [31:0] Code,
  input  [31:0] PC4,
  output Sregwrite,
  output Smemwrite,
  output Smemread,
  output [3:0] SALUop,
  output Sjump,
  output Sbranch,
  output Smemtoreg,
  output Salusrc,
  output Sregdst,
  output [31:0] SA,
  output [31:0] SB,
  output [31:0] SImmediate,
  output [31:0] SCode,
  output [31:0] SPC4
);

  Register #(.width(1)) register_1 (.D(regwrite), .en(1'b1), .clk(Clk), .Q(Sregwrite));  // open: clr
  Register #(.width(1)) register_2 (.D(memwrite), .en(1'b1), .clk(Clk), .Q(Smemwrite));  // open: clr
  Register #(.width(1)) register_3 (.D(memread), .en(1'b1), .clk(Clk), .Q(Smemread));  // open: clr
  Register #(.width(4)) register_4 (.D(ALUOp), .en(1'b1), .clk(Clk), .Q(SALUop));  // open: clr
  Register #(.width(1)) register_5 (.D(jump), .en(1'b1), .clk(Clk), .Q(Sjump));  // open: clr
  Register #(.width(1)) register_6 (.D(branch), .en(1'b1), .clk(Clk), .Q(Sbranch));  // open: clr
  Register #(.width(1)) register_7 (.D(momtoreg), .en(1'b1), .clk(Clk), .Q(Smemtoreg));  // open: clr
  Register #(.width(1)) register_8 (.D(alusrc), .en(1'b1), .clk(Clk), .Q(Salusrc));  // open: clr
  Register #(.width(1)) register_9 (.D(regdst), .en(1'b1), .clk(Clk), .Q(Sregdst));  // open: clr
  Register #(.width(32)) register_10 (.D(A), .en(1'b1), .clk(Clk), .Q(SA));  // open: clr
  Register #(.width(32)) register_11 (.D(B), .en(1'b1), .clk(Clk), .Q(SB));  // open: clr
  Register #(.width(32)) register_12 (.D(Immediate), .en(1'b1), .clk(Clk), .Q(SImmediate));  // open: clr
  Register #(.width(32)) register_13 (.D(Code), .en(1'b1), .clk(Clk), .Q(SCode));  // open: clr
  Register #(.width(32)) register_14 (.D(PC4), .en(1'b1), .clk(Clk), .Q(SPC4));  // open: clr
endmodule

module EXE_MEM (
  input  Clk,
  input  regwrite,
  input  jumpR,
  input  memtoreg,
  input  memwrite,
  input  memread,
  input  [31:0] Addrs,
  input  [31:0] DWrite,
  input  [4:0] RWrite,
  input  [31:0] PC4,
  input  [4:0] RegSel,
  output Sregwrite,
  output SjumpR,
  output Smemtoreg,
  output Smemwrite,
  output Smemread,
  output [31:0] SAddrs,
  output [31:0] SDWrite,
  output [4:0] SRWrite,
  output [31:0] SPC4,
  output [4:0] SRegSel
);

  Register #(.width(1)) register_1 (.D(regwrite), .en(1'b1), .clk(Clk), .Q(Sregwrite));  // open: clr
  Register #(.width(1)) register_2 (.D(jumpR), .en(1'b1), .clk(Clk), .Q(SjumpR));  // open: clr
  Register #(.width(1)) register_3 (.D(memtoreg), .en(1'b1), .clk(Clk), .Q(Smemtoreg));  // open: clr
  Register #(.width(1)) register_4 (.D(memwrite), .en(1'b1), .clk(Clk), .Q(Smemwrite));  // open: clr
  Register #(.width(1)) register_5 (.D(memread), .en(1'b1), .clk(Clk), .Q(Smemread));  // open: clr
  Register #(.width(32)) register_6 (.D(Addrs), .en(1'b1), .clk(Clk), .Q(SAddrs));  // open: clr
  Register #(.width(32)) register_7 (.D(DWrite), .en(1'b1), .clk(Clk), .Q(SDWrite));  // open: clr
  Register #(.width(5)) register_8 (.D(RWrite), .en(1'b1), .clk(Clk), .Q(SRWrite));  // open: clr
  Register #(.width(32)) register_9 (.D(PC4), .en(1'b1), .clk(Clk), .Q(SPC4));  // open: clr
  Register #(.width(5)) register_10 (.D(RegSel), .en(1'b1), .clk(Clk), .Q(SRegSel));  // open: clr
endmodule

module MEM_WB (
  input  Clk,
  input  regwrite,
  input  jumpR,
  input  memtoreg,
  input  [31:0] DataR,
  input  [31:0] Rst,
  input  [4:0] RWrite,
  input  [31:0] PC4,
  input  [4:0] RegSel,
  output Sregwrite,
  output SjumpR,
  output Smemtoreg,
  output [31:0] SDataR,
  output [31:0] SRst,
  output [4:0] SRWrite,
  output [31:0] SPC4,
  output [4:0] SRegSel
);

  Register #(.width(1)) register_1 (.D(regwrite), .en(1'b1), .clk(Clk), .Q(Sregwrite));  // open: clr
  Register #(.width(1)) register_2 (.D(jumpR), .en(1'b1), .clk(Clk), .Q(SjumpR));  // open: clr
  Register #(.width(1)) register_3 (.D(memtoreg), .en(1'b1), .clk(Clk), .Q(Smemtoreg));  // open: clr
  Register #(.width(32)) register_4 (.D(DataR), .en(1'b1), .clk(Clk), .Q(SDataR));  // open: clr
  Register #(.width(32)) register_5 (.D(Rst), .en(1'b1), .clk(Clk), .Q(SRst));  // open: clr
  Register #(.width(5)) register_6 (.D(RWrite), .en(1'b1), .clk(Clk), .Q(SRWrite));  // open: clr
  Register #(.width(32)) register_7 (.D(PC4), .en(1'b1), .clk(Clk), .Q(SPC4));  // open: clr
  Register #(.width(5)) register_8 (.D(RegSel), .en(1'b1), .clk(Clk), .Q(SRegSel));  // open: clr
endmodule

module Forwarding (
  input  [4:0] Rs,
  input  [4:0] Rt,
  input  [4:0] RdExMem,
  input  [4:0] RdMemWb,
  input  RWExMem,
  input  RWMemWb,
  output [1:0] RsSelector,
  output [1:0] RtSelector
);

  ForwardingLogic RsForward (
    .RWExMem(RWExMem), .RWMemWb(RWMemWb), .RdExMem(RdExMem), .Rs(Rs), .RdMemWb(RdMemWb), .Selector(RsSelector));
  ForwardingLogic forwardinglogic_1 (
    .RWExMem(RWExMem), .RWMemWb(RWMemWb), .RdExMem(RdExMem), .Rs(Rt), .RdMemWb(RdMemWb), .Selector(RtSelector));
endmodule

module ForwardingLogic (
  input  RWExMem,
  input  RWMemWb,
  input  [4:0] RdExMem,
  input  [4:0] Rs,
  input  [4:0] RdMemWb,
  output [1:0] Selector
);

  wire and_1_out, and_2_out, and_3_out, and_4_out, and_5_out, comparator_1_eq, comparator_2_eq,
       comparator_3_eq, comparator_4_eq, not_1_out, not_2_out, or_1_out;
  wire [1:0] bit_extender_1_out, bit_extender_2_out, or_2_out, shifter_1_out;

  Comparator #(.width(5), .mode("unsigned")) comparator_1 (
    .a(RdExMem), .b({5{1'b0}}), .eq(comparator_1_eq));  // open: gt, lt
  Comparator #(.width(5), .mode("unsigned")) comparator_2 (.a(RdExMem), .b(Rs), .eq(comparator_2_eq));  // open: gt, lt
  Comparator #(.width(5), .mode("unsigned")) comparator_3 (.a(Rs), .b(RdMemWb), .eq(comparator_3_eq));  // open: gt, lt
  Comparator #(.width(5), .mode("unsigned")) comparator_4 (
    .a(RdMemWb), .b({5{1'b0}}), .eq(comparator_4_eq));  // open: gt, lt
  not not_1 (not_1_out, comparator_1_eq);
  not not_2 (not_2_out, comparator_4_eq);
  and and_1 (and_1_out, not_1_out, ~comparator_3_eq, comparator_2_eq);  // AND_Gate
  and and_2 (and_2_out, comparator_3_eq, ~comparator_2_eq, not_2_out);  // AND_Gate
  and and_3 (and_3_out, comparator_2_eq, comparator_3_eq, not_1_out, not_2_out);
  and and_4 (and_4_out, RWMemWb, and_2_out);
  or or_1 (or_1_out, and_1_out, and_3_out);
  and and_5 (and_5_out, RWExMem, or_1_out);
  assign bit_extender_1_out = {{1{1'b0}}, and_5_out};  // Bit_Extender bit_extender_1
  assign bit_extender_2_out = {{1{1'b0}}, and_4_out};  // Bit_Extender bit_extender_2
  Shifter #(.width(2)) shifter_1 (.in(bit_extender_2_out), .\dist (1'b1), .out(shifter_1_out));
  assign or_2_out = bit_extender_1_out | shifter_1_out;  // OR_Gate or_2, 2 bits wide
  Multiplexer #(.select(2), .width(2), .enable("false")) multiplexer_1 (
    .in0(2'b00), .in1(2'b01), .in2(2'b10), .in3(2'b00), .out(Selector), .sel(or_2_out));
endmodule

module count (
  input  in_1,
  output [15:0] out_2
);

  wire button_1_out;
  wire [15:0] adder_1_out;

  Register #(.width(16), .trigger("falling")) register_1 (
    .D(adder_1_out), .en(1'b1), .clk(in_1), .Q(out_2), .clr(button_1_out));
  Button button_1 (.out(button_1_out));
  Adder #(.width(16)) adder_1 (.a(16'h1), .b(out_2), .out(adder_1_out));  // open: cin, cout
endmodule
