// Logisim project pipelinefin.circ as structural Verilog: 10 circuits, main circuit main
module main (
);

  wire clock_1_out, decode_1_oload, decode_1_omuxb, decode_1_omuxreg, decode_1_ostore, decode_1_owb,
       decode_1_owe, exe_1_oload, exe_1_ostore, exe_1_owb, exe_1_owe, exe_mem_1_out_9, exe_mem_1_out_10,
       exe_mem_1_out_11, exe_mem_1_out_12, id_exe_1_out_11, id_exe_1_out_12, id_exe_1_out_13,
       id_exe_1_out_14, id_exe_1_out_15, id_exe_1_out_16, mem_1_owb, mem_1_owe, mem_wb_1_out_7,
       mem_wb_1_out_8, wb_1_owe;
  wire [4:0] exe_1_orw, exe_mem_1_out_15, mem_1_orw, mem_wb_1_out_11, wb_1_orw;
  wire [31:0] decode_1_oopcode, decode_1_rs, decode_1_rt, exe_1_orst, exe_1_ort, exe_mem_1_out_13,
       exe_mem_1_out_14, fetch_1_opcode, id_exe_1_out_17, id_exe_1_out_18, id_exe_1_out_19, if_id_1_oopcode,
       mem_1_oldata, mem_1_orst, mem_wb_1_out_9, mem_wb_1_out_10, wb_1_wdata;

  Clock clock_1 (.out(clock_1_out));
  Fetch fetch_1 (.Clk(clock_1_out), .Opcode(fetch_1_opcode));
  IF_ID if_id_1 (.Clk(clock_1_out), .Opcode(fetch_1_opcode), .oOpcode(if_id_1_oopcode));
  Decode decode_1 (
    .Clk(clock_1_out), .Opcode(if_id_1_oopcode), .DataWB(wb_1_wdata), .we(wb_1_owe), .WReg(wb_1_orw),
    .omuxreg(decode_1_omuxreg), .omuxb(decode_1_omuxb), .owe(decode_1_owe), .ostore(decode_1_ostore),
    .oload(decode_1_oload), .owb(decode_1_owb), .RS(decode_1_rs), .RT(decode_1_rt), .oopcode(decode_1_oopcode));
  ID_EXE id_exe_1 (
    .Clk(clock_1_out), .in_2(decode_1_omuxreg), .in_3(decode_1_omuxb), .in_4(decode_1_owe),
    .in_5(decode_1_ostore), .in_6(decode_1_oload), .in_7(decode_1_owb), .in_8(decode_1_rs),
    .in_9(decode_1_rt), .in_10(decode_1_oopcode), .out_11(id_exe_1_out_11), .out_12(id_exe_1_out_12),
    .out_13(id_exe_1_out_13), .out_14(id_exe_1_out_14), .out_15(id_exe_1_out_15), .out_16(id_exe_1_out_16),
    .out_17(id_exe_1_out_17), .out_18(id_exe_1_out_18), .out_19(id_exe_1_out_19));
  Exe exe_1 (
    .muxreg(id_exe_1_out_11), .muxb(id_exe_1_out_12), .we(id_exe_1_out_13), .store(id_exe_1_out_14),
    .load(id_exe_1_out_15), .wb(id_exe_1_out_16), .RS(id_exe_1_out_17), .RT(id_exe_1_out_18),
    .opcode(id_exe_1_out_19), .oWe(exe_1_owe), .oStore(exe_1_ostore), .oLoad(exe_1_oload), .oWb(exe_1_owb),
    .oRst(exe_1_orst), .oRT(exe_1_ort), .oRW(exe_1_orw));
  EXE_MEM exe_mem_1 (
    .in_1(clock_1_out), .in_2(exe_1_owe), .in_3(exe_1_ostore), .in_4(exe_1_oload), .in_5(exe_1_owb),
    .in_6(exe_1_orst), .in_7(exe_1_ort), .in_8(exe_1_orw), .out_9(exe_mem_1_out_9),
    .out_10(exe_mem_1_out_10), .out_11(exe_mem_1_out_11), .out_12(exe_mem_1_out_12),
    .out_13(exe_mem_1_out_13), .out_14(exe_mem_1_out_14), .out_15(exe_mem_1_out_15));
  Mem mem_1 (
    .Clk(clock_1_out), .we(exe_mem_1_out_9), .store(exe_mem_1_out_10), .load(exe_mem_1_out_11),
    .wb(exe_mem_1_out_12), .Rst(exe_mem_1_out_13), .RT(exe_mem_1_out_14), .RW(exe_mem_1_out_15),
    .oWe(mem_1_owe), .oWb(mem_1_owb), .oRst(mem_1_orst), .oLData(mem_1_oldata), .oRw(mem_1_orw));
  MEM_WB mem_wb_1 (
    .in_1(clock_1_out), .in_2(mem_1_owe), .in_3(mem_1_owb), .in_4(mem_1_orst), .in_5(mem_1_oldata),
    .in_6(mem_1_orw), .out_7(mem_wb_1_out_7), .out_8(mem_wb_1_out_8), .out_9(mem_wb_1_out_9),
    .out_10(mem_wb_1_out_10), .out_11(mem_wb_1_out_11));
  Wb wb_1 (
    .we(mem_wb_1_out_7), .wb(mem_wb_1_out_8), .Rst(mem_wb_1_out_9), .LData(mem_wb_1_out_10),
    .Rw(mem_wb_1_out_11), .oWe(wb_1_owe), .WData(wb_1_wdata), .oRw(wb_1_orw));
endmodule

module Fetch (
  input  Clk,
  output [31:0] Opcode
);

  wire button_1_out;
  wire [31:0] adder_1_out, register_1_q;

  Register #(.width(32), .trigger("falling")) register_1 (
    .D(adder_1_out), .en(1'b1), .clk(Clk), .Q(register_1_q), .clr(button_1_out));
  Button button_1 (.out(button_1_out));
  // MIPSProgramROM mipsprogramrom_1: pin names not known; wires that end beside it: register_1_q, Opcode
  Adder #(.width(32)) adder_1 (.a(32'h4), .b(register_1_q), .out(adder_1_out));  // open: cin, cout

  // Notes on the sheet:
  //   contents of mipsprogramrom_1 (hex, n*v repeats v):
  //   addiu $t0, $zero, 5 addiu $t1, $zero, 10  # sw , word address (24bit) 1 in RAM  = 1  sw $t1,
  //   0($zero) lw $t3, 0($zero)        # $t3 = 10
endmodule

module Decode (
  input  Clk,
  input  [31:0] Opcode,
  input  [31:0] DataWB,
  input  we,
  input  [4:0] WReg,
  output omuxreg,
  output omuxb,
  output owe,
  output ostore,
  output oload,
  output owb,
  output [31:0] RS,
  output [31:0] RT,
  output [31:0] oopcode
);

  ROM #(.addrWidth(6), .dataWidth(6)) rom_1 (.addr(Opcode[31:26]), .data({owb, oload, ostore, owe, omuxb, omuxreg}));
  // RegisterFile #(.trigger("falling")) registerfile_1: pin names not known; wires that end beside it: Opcode[15:0], DataWB, Clk, we, WReg, Opcode[25:21], Opcode[20:16], RS, RT

  assign oopcode = Opcode;

  // Other names for the same wires on the sheet: muxreg = omuxreg; muxb = omuxb; we_t = owe; store = ostore;
  //   load = oload; wb = owb

  // Notes on the sheet:
  //   contents of rom_1 (hex, n*v repeats v):
  //   25 8*0 26 25*0 16 7*0 a
  //   rs
  //   rt
endmodule

module Exe (
  input  muxreg,
  input  muxb,
  input  we,
  input  store,
  input  load,
  input  wb,
  input  [31:0] RS,
  input  [31:0] RT,
  input  [31:0] opcode,
  output oWe,
  output oStore,
  output oLoad,
  output oWb,
  output [31:0] oRst,
  output [31:0] oRT,
  output [4:0] oRW
);

  wire [31:0] bit_extender_1_out, multiplexer_2_out;

  assign bit_extender_1_out = {{16{opcode[15]}}, opcode[15:0]};  // Bit_Extender bit_extender_1
  Multiplexer #(.width(5), .enable("false")) multiplexer_1 (
    .in0(opcode[20:16]), .in1(opcode[15:11]), .out(oRW), .sel(muxreg));
  Multiplexer #(.width(32), .enable("false")) multiplexer_2 (
    .in0(RT), .in1(bit_extender_1_out), .out(multiplexer_2_out), .sel(muxb));
  // Mips_ALU mips_alu_1: pin names not known; wires that end beside it: RS, multiplexer_2_out, 4'b0010, oRst

  assign oLoad = load;
  assign oRT = RT;
  assign oStore = store;
  assign oWb = wb;
  assign oWe = we;

  // Notes on the sheet:
  //   rs
  //   rt
endmodule

module Mem (
  input  Clk,
  input  we,
  input  store,
  input  load,
  input  wb,
  input  [31:0] Rst,
  input  [31:0] RT,
  input  [4:0] RW,
  output oWe,
  output oWb,
  output [31:0] oRst,
  output [31:0] oLData,
  output [4:0] oRw
);

  // MIPS_RAM #(.addrWidth(24)) mips_ram_1: pin names not known; wires that end beside it: Rst[23:0], RT, store, Clk, load, oLData

  assign oRst = Rst;
  assign oRw = RW;
  assign oWb = wb;
  assign oWe = we;
endmodule

module Wb (
  input  we,
  input  wb,
  input  [31:0] Rst,
  input  [31:0] LData,
  input  [4:0] Rw,
  output oWe,
  output [31:0] WData,
  output [4:0] oRw
);

  Multiplexer #(.width(32), .enable("false")) multiplexer_1 (.in0(LData), .in1(Rst), .out(WData), .sel(wb));

  assign oRw = Rw;
  assign oWe = we;
endmodule

module IF_ID (
  input  Clk,
  input  [31:0] Opcode,
  output [31:0] oOpcode
);

  Register #(.width(32)) register_1 (.D(Opcode), .en(1'b1), .clk(Clk), .Q(oOpcode));  // open: clr
endmodule

module ID_EXE (
  input  Clk,
  input  in_2,
  input  in_3,
  input  in_4,
  input  in_5,
  input  in_6,
  input  in_7,
  input  [31:0] in_8,
  input  [31:0] in_9,
  input  [31:0] in_10,
  output out_11,
  output out_12,
  output out_13,
  output out_14,
  output out_15,
  output out_16,
  output [31:0] out_17,
  output [31:0] out_18,
  output [31:0] out_19
);

  Register #(.width(1)) register_1 (.D(in_2), .en(1'b1), .clk(Clk), .Q(out_11));  // open: clr
  Register #(.width(1)) register_2 (.D(in_3), .en(1'b1), .clk(Clk), .Q(out_12));  // open: clr
  Register #(.width(1)) register_3 (.D(in_4), .en(1'b1), .clk(Clk), .Q(out_13));  // open: clr
  Register #(.width(1)) register_4 (.D(in_5), .en(1'b1), .clk(Clk), .Q(out_14));  // open: clr
  Register #(.width(1)) register_5 (.D(in_6), .en(1'b1), .clk(Clk), .Q(out_15));  // open: clr
  Register #(.width(1)) register_6 (.D(in_7), .en(1'b1), .clk(Clk), .Q(out_16));  // open: clr
  Register #(.width(32)) register_7 (.D(in_8), .en(1'b1), .clk(Clk), .Q(out_17));  // open: clr
  Register #(.width(32)) register_8 (.D(in_9), .en(1'b1), .clk(Clk), .Q(out_18));  // open: clr
  Register #(.width(32)) register_9 (.D(in_10), .en(1'b1), .clk(Clk), .Q(out_19));  // open: clr
endmodule

module EXE_MEM (
  input  in_1,
  input  in_2,
  input  in_3,
  input  in_4,
  input  in_5,
  input  [31:0] in_6,
  input  [31:0] in_7,
  input  [4:0] in_8,
  output out_9,
  output out_10,
  output out_11,
  output out_12,
  output [31:0] out_13,
  output [31:0] out_14,
  output [4:0] out_15
);

  Register #(.width(1)) register_1 (.D(in_2), .en(1'b1), .clk(in_1), .Q(out_9));  // open: clr
  Register #(.width(1)) register_2 (.D(in_3), .en(1'b1), .clk(in_1), .Q(out_10));  // open: clr
  Register #(.width(1)) register_3 (.D(in_4), .en(1'b1), .clk(in_1), .Q(out_11));  // open: clr
  Register #(.width(1)) register_4 (.D(in_5), .en(1'b1), .clk(in_1), .Q(out_12));  // open: clr
  Register #(.width(32)) register_5 (.D(in_6), .en(1'b1), .clk(in_1), .Q(out_13));  // open: clr
  Register #(.width(32)) register_6 (.D(in_7), .en(1'b1), .clk(in_1), .Q(out_14));  // open: clr
  Register #(.width(5)) register_7 (.D(in_8), .en(1'b1), .clk(in_1), .Q(out_15));  // open: clr
endmodule

module MEM_WB (
  input  in_1,
  input  in_2,
  input  in_3,
  input  [31:0] in_4,
  input  [31:0] in_5,
  input  [4:0] in_6,
  output out_7,
  output out_8,
  output [31:0] out_9,
  output [31:0] out_10,
  output [4:0] out_11
);

  Register #(.width(1)) register_1 (.D(in_2), .en(1'b1), .clk(in_1), .Q(out_7));  // open: clr
  Register #(.width(1)) register_2 (.D(in_3), .en(1'b1), .clk(in_1), .Q(out_8));  // open: clr
  Register #(.width(32)) register_3 (.D(in_4), .en(1'b1), .clk(in_1), .Q(out_9));  // open: clr
  Register #(.width(32)) register_4 (.D(in_5), .en(1'b1), .clk(in_1), .Q(out_10));  // open: clr
  Register #(.width(5)) register_5 (.D(in_6), .en(1'b1), .clk(in_1), .Q(out_11));  // open: clr
endmodule
