// Logisim project singlefin.circ as structural Verilog: 1 circuit, main circuit main
module main (
);

  wire button_1_out, clock_1_out, load, muxb, muxreg, registerfile_1_p6, store, wb, we;
  wire [4:0] multiplexer_1_out;
  wire [5:0] mipsprogramrom_1_p2_2;
  wire [25:0] mipsprogramrom_1_p2;
  wire [31:0] adder_1_out, bit_extender_1_out, mips_alu_1_p4, mips_ram_1_p6, multiplexer_2_out, register_1_q,
       registerfile_1_p1, registerfile_1_p7;

  ROM #(.addrWidth(6), .dataWidth(6)) rom_1 (.addr(mipsprogramrom_1_p2_2), .data({wb, load, store, we, muxb, muxreg}));
  Clock clock_1 (.out(clock_1_out));
  Register #(.width(32)) register_1 (
    .D(adder_1_out), .en(1'b1), .clk(clock_1_out), .Q(register_1_q), .clr(button_1_out));
  Button button_1 (.out(button_1_out));
  Adder #(.width(32)) adder_1 (.a(32'h4), .b(register_1_q), .out(adder_1_out));  // open: cin, cout
  // MIPSProgramROM mipsprogramrom_1: pin names not known; wires that end beside it: register_1_q, {mipsprogramrom_1_p2_2, mipsprogramrom_1_p2}, clock_1_out
  Multiplexer #(.width(5), .enable("false")) multiplexer_1 (
    .in0(mipsprogramrom_1_p2[20:16]), .in1(mipsprogramrom_1_p2[15:11]), .out(multiplexer_1_out), .sel(muxreg));
  // RegisterFile registerfile_1: pin names not known; wires that end beside it: registerfile_1_p1, we, multiplexer_1_out, mipsprogramrom_1_p2[25:21], mipsprogramrom_1_p2[20:16], registerfile_1_p6, registerfile_1_p7
  assign bit_extender_1_out = {{16{mipsprogramrom_1_p2[15]}}, mipsprogramrom_1_p2[15:0]};  // Bit_Extender bit_extender_1
  Multiplexer #(.width(32), .enable("false")) multiplexer_2 (
    .in0(registerfile_1_p7), .in1(bit_extender_1_out), .out(multiplexer_2_out), .sel(muxb));
  // Mips_ALU mips_alu_1: pin names not known; wires that end beside it: registerfile_1_p6, multiplexer_2_out, 4'b0010, mips_alu_1_p4
  // MIPS_RAM #(.addrWidth(24)) mips_ram_1: pin names not known; wires that end beside it: mips_alu_1_p4[23:0], registerfile_1_p7, store, clock_1_out, load, mips_ram_1_p6
  Multiplexer #(.width(32), .enable("false")) multiplexer_3 (
    .in0(mips_ram_1_p6), .in1(mips_alu_1_p4), .out(registerfile_1_p1), .sel(wb));

  // Notes on the sheet:
  //   contents of rom_1 (hex, n*v repeats v):
  //   25 8*0 26 25*0 16 7*0 a
  //   contents of mipsprogramrom_1 (hex, n*v repeats v):
  //   addiu $t0, $zero, 5 addiu $t1, $zero, 10  # sw , word address (24bit) 1 in RAM  = 1  sw $t1,
  //   0($zero) lw $t3, 0($zero)        # $t3 = 10
  //   rt
  //   rd
  //   rs
  //   rt
endmodule
